# Fritzing sketch esm-board-OSH-version (saved by Fritzing 0.9.3b)
circuit board: 3.76715cm x 2.06939cm
breadboards: 1

parts:
  ble_nano1 = female pin header, 6 pins [form="♀ (female)"]
  J1 = female pin header, 6 pins [form="♀ (female)"]
  BAT6 = Battery Holders [package=battcon_12mm]
  pot5 = female pin header, 3 pins [form="♀ (female)"]
  10k3 = Resistor [tolerance=±5% resistance=10k package=THT]
  led = female pin header, 3 pins [form="♀ (female)"]

nets:
  N1: ble_nano1.pin5, led.pin3
  N2: ble_nano1.pin6, BAT6.+, pot5.pin1
  N3: J1.pin2, BAT6.-, pot5.pin3, 10k3.Pin_0, led.pin1
  N4: J1.pin3, led.pin2
  N5: J1.pin4, pot5.pin2, 10k3.Pin_1
